# Fritzing sketch Capstone (saved by Fritzing 0.9.3b)
circuit board: 3.77198cm x 4.52cm
breadboards: 1

parts:
  Mic = Adafruit MAX9814 Electret Microphone Amplifier [part_number="Adafruit #1713"]
  Pro_mini = Arduino Pro Mini (5V)
  Voltage_REG = LD33 Low-Dropout Voltage Regulator
  Toggle = SWITCH-DPDT [package=os]
  Water_Pump = female pin header, 2 pins [form="♀ (female)"]
  Power_Supply = female pin header, 2 pins [form="♀ (female)"]
  NeoPix = female pin header, 3 pins [form="♀ (female)"]

nets:
  GND: Mic.GND, Pro_mini.GND, Toggle.2, Power_Supply.pin1, NeoPix.pin1
  VDD: Mic.VDD, Pro_mini.VCC, Voltage_REG.Vout, NeoPix.pin3
  N1: Mic.OUTPUT, Pro_mini.A1
  N2: Pro_mini.D6, NeoPix.pin2
  N3: Voltage_REG.GND, Toggle.4, Water_Pump.pin1
  N4: Voltage_REG.Vin, Toggle.1, Water_Pump.pin2
  N5: Toggle.5, Power_Supply.pin2

notes:
  Water Pump

custom parts:
  Adafruit MAX9814 Electret Microphone Amplifier: Add an ear to your project with this well-designed electret microphone amplifier with AGC. This fully assembled and tested board comes with a 20-20KHz electret microphone soldered on. For the amplification, we use the Maxim MAX9814, a specialty chip that is designed for amplifying electret microphones in situations where the loudness of the audio isn't predictable. This fancy microphone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
