# Fritzing sketch Fritzing Project (saved by Fritzing 0.9.3b)
circuit board: 2.5cm x 2.5cm
breadboards: 1

parts:
  Tiny85 = IC, DIP package, 8 pins [chip_label=IC]
  I/O = Toggle Switch [package=THT]
  Pot = TRIMPOT [package=3362u-2]
  Piezo = Piezo Speaker
  BAT = Battery Holders [package=battcom_20mm_pth]
  Tog = Toggle Switch [package=THT]
  10K = Resistor [tolerance=±5% resistance=10k package=THT]

nets:
  N1: Tiny85.pin4, Pot.CW, Piezo.pin2, BAT.-, Tog.COM, Tog.L2
  N2: Tiny85.pin5, Piezo.pin1
  N3: Tiny85.pin6, Tog.L1, 10K.Pin_0
  N4: Tiny85.pin7, Pot.WIPER
  N5: Tiny85.pin8, I/O.COM, I/O.L2, Pot.CCW, 10K.Pin_1
  N6: I/O.L1, BAT.+
