# Fritzing sketch Full PCB Design (saved by Fritzing 0.9.3b)
circuit board: 2.196cm x 3.48198cm
circuit board: 5.06259cm x 5.63851cm
circuit board: 0.957151cm x 1.46173cm
breadboards: 1

parts:
  U1 = LIPO-1000mAh [package=lipo-1000]  # not connected
  Part6 = PowerBoost 500 Charger  # not connected
  Part7 = PowerBoost 500 Charger  # not connected
  Part8 = PowerBoost 500 Charger  # not connected
  Pro_Mini = Arduino Pro Mini (5V)
  Power_in = female pin header, 2 pins [form="♀ (female)"]
  Buttons = female pin header, 5 pins [form="♀ (female)"]
  J4 = female pin header, 5 pins [form="♀ (female)"]
  S4 = Pushbutton [package="[THT]"]
  S5 = Pushbutton [package="[THT]"]
  S6 = Pushbutton [package="[THT]"]
  R11 = Resistor [tolerance=±5% resistance=10k package=THT]
  R12 = Resistor [tolerance=±5% resistance=10k package=THT]
  R13 = Resistor [tolerance=±5% resistance=10k package=THT]
  M1 = female pin header, 5 pins [form="♀ (female)"]
  M2 = female pin header, 5 pins [form="♀ (female)"]
  M4 = female pin header, 5 pins [form="♀ (female)"]
  M3 = female pin header, 5 pins [form="♀ (female)"]
  M_Power_in = female pin header, 4 pins [form="♀ (female)"]
  Screen = female pin header, 10 pins [form="♀ (female)"]
  S7 = Toggle Switch [package=THT]
  S8 = Toggle Switch [package=THT]
  S9 = Toggle Switch [package=THT]

nets:
  N1: Pro_Mini.GND, Power_in.pin1, Buttons.pin2, M1.pin4, M2.pin4, M4.pin4, M3.pin4, Screen.pin1
  N2: Pro_Mini.RAW, Power_in.pin2
  N3: Pro_Mini.VCC, Buttons.pin1, Screen.pin2
  N4: Pro_Mini.A3, M1.pin5
  N5: Pro_Mini.A2, M2.pin5
  N6: Pro_Mini.A1, M3.pin5
  N7: Pro_Mini.A0, M4.pin5
  N8: Pro_Mini.SCK, Screen.pin9
  N9: Pro_Mini.MISO, Screen.pin8
  N10: Pro_Mini.MOSI, Screen.pin7
  N11: Pro_Mini.D10, Screen.pin6
  N12: Pro_Mini.D9, Screen.pin3
  N13: Pro_Mini.D8, Screen.pin4
  N14: Pro_Mini.D7, Buttons.pin5
  N15: Pro_Mini.D6, Buttons.pin4
  N16: Pro_Mini.D5, Buttons.pin3
  N17: J4.pin1, S6.Pin_3, S6.Pin_4
  N18: J4.pin2, S5.Pin_3, S5.Pin_4
  N19: J4.pin3, S4.Pin_3, S4.Pin_4
  N20: J4.pin4, S4.Pin_1, S4.Pin_2, S5.Pin_1, S5.Pin_2, S6.Pin_1, S6.Pin_2, R11.Pin_0, R12.Pin_0, R13.Pin_0
  N21: J4.pin5, R11.Pin_1, R12.Pin_1, R13.Pin_1
  N22: M1.pin1, M2.pin1, M4.pin1, M3.pin1, M_Power_in.pin1
  N23: M1.pin2, M2.pin2, M4.pin2, M3.pin2, M_Power_in.pin2, M_Power_in.pin3
  N24: M1.pin3, M2.pin3, M4.pin3, M3.pin3, M_Power_in.pin4
  N25: S7.COM, S7.L2
  N26: S8.COM, S8.L2
  N27: S9.COM, S9.L2

notes:
  4 Muscle Sensors
